// Logisim project cpu8b.circ as structural Verilog: 20 circuits, main circuit main
module main (
  input  in_1,
  input  in_2,
  input  in_3,
  output [15:0] out_4,
  output [7:0] out_5,
  output [7:0] out_6,
  output [7:0] out_7,
  output [7:0] out_8,
  output [7:0] out_9
);

  wire alu8b_1_zero, and_1_out, clock_1_out, controlunit_1_alusrc, controlunit_1_branch, controlunit_1_memr,
       controlunit_1_memtoreg, controlunit_1_memw, controlunit_1_regwrite;
  wire [1:0] controlunit_1_aluctrl, controlunit_1_ard, controlunit_1_ars1, controlunit_1_ars2;
  wire [7:0] alu8b_1_out, Branch_logic_out_4, controlunit_1_imm, mux8b_1_out_4, mux8b_2_out_4, ram_2_data,
       Registri_rs1, Registri_rs2;

  Clock clock_1 (.out(clock_1_out));
  Hex_Digit_Display hex_digit_display_1 (.value(out_5[7:4]));  // open: dp
  Hex_Digit_Display hex_digit_display_2 (.value(out_5[3:0]));  // open: dp
  Reg PC (.Address(Branch_logic_out_4), .Clock(clock_1_out), .Enable(in_2), .out_5(out_5), .Reset(in_3));
  BranchLogic Branch_logic (.Address(out_5), .Imm(controlunit_1_imm), .out_4(Branch_logic_out_4), .Branch(and_1_out));
  Hex_Digit_Display hex_digit_display_3 (.value(out_6[7:4]));  // open: dp
  and and_1 (and_1_out, alu8b_1_zero, controlunit_1_branch);
  RAM #(.dataWidth(16)) ram_1 (.addr(out_5), .data(out_4), .clk(clock_1_out), .ld(1'b1));  // open: sel, clr
  Hex_Digit_Display hex_digit_display_4 (.value(out_6[3:0]));  // open: dp
  Hex_Digit_Display hex_digit_display_5 (.value(out_7[3:0]));  // open: dp
  Hex_Digit_Display hex_digit_display_6 (.value(out_7[7:4]));  // open: dp
  Registri Registri (
    .Reset(in_1), .Clock(clock_1_out), .RD(mux8b_2_out_4), .RS1(Registri_rs1), .RS2(Registri_rs2),
    .x0(out_6), .x1(out_7), .x2(out_8), .x3(out_9), .RegWrite(controlunit_1_regwrite),
    .ARD(controlunit_1_ard), .ARS1(controlunit_1_ars1), .ARS2(controlunit_1_ars2));
  ControlUnit controlunit_1 (
    .in_1(out_4), .Imm(controlunit_1_imm), .RegWrite(controlunit_1_regwrite), .ARD(controlunit_1_ard),
    .ARS1(controlunit_1_ars1), .ARS2(controlunit_1_ars2), .ALUctrl(controlunit_1_aluctrl),
    .Branch(controlunit_1_branch), .ALUsrc(controlunit_1_alusrc), .MemR(controlunit_1_memr),
    .MemToReg(controlunit_1_memtoreg), .MemW(controlunit_1_memw));
  Hex_Digit_Display hex_digit_display_7 (.value(out_8[7:4]));  // open: dp
  Hex_Digit_Display hex_digit_display_8 (.value(out_8[3:0]));  // open: dp
  Hex_Digit_Display hex_digit_display_9 (.value(out_9[3:0]));  // open: dp
  Hex_Digit_Display hex_digit_display_10 (.value(out_9[7:4]));  // open: dp
  MUX8b mux8b_1 (.in_1(Registri_rs2), .in_2(controlunit_1_imm), .in_3(controlunit_1_alusrc), .out_4(mux8b_1_out_4));
  ALU8b alu8b_1 (
    .A(Registri_rs1), .B(mux8b_1_out_4), .Zero(alu8b_1_zero), .Out(alu8b_1_out), .OP(controlunit_1_aluctrl));  // open: Co, Over
  RAM #(.bus("separate")) ram_2 (
    .addr(alu8b_1_out), .din(Registri_rs2), .data(ram_2_data), .str(controlunit_1_memw), .clk(clock_1_out),
    .ld(controlunit_1_memr));  // open: sel, clr
  MUX8b mux8b_2 (.in_1(alu8b_1_out), .in_2(ram_2_data), .in_3(controlunit_1_memtoreg), .out_4(mux8b_2_out_4));

  // Other names for the same wires on the sheet: PC[7:0] = out_5; x0[7:0] = out_6; x1[7:0] = out_7; x2[7:0] = out_8;
  //   x3[7:0] = out_9
endmodule

module HA (
  input  in_1,
  input  in_2,
  output out_3,
  output out_4
);

  and and_1 (out_4, in_1, in_2);
  xor xor_1 (out_3, in_1, in_2);
endmodule

module FA (
  input  in_1,
  input  in_2,
  input  in_3,
  output out_4,
  output out_5
);

  wire ha_1_out_3, ha_1_out_4, ha_2_out_4;

  HA ha_1 (.in_1(in_2), .in_2(in_3), .out_4(ha_1_out_4), .out_3(ha_1_out_3));
  or or_1 (out_5, ha_1_out_4, ha_2_out_4);
  HA ha_2 (.in_1(ha_1_out_3), .in_2(in_1), .out_4(ha_2_out_4), .out_3(out_4));
endmodule

module Reg (
  input  [7:0] Address,
  input  Clock,
  input  Enable,
  input  Reset,
  output [7:0] out_5
);

  D_Flip_Flop d_ff_1 (.clk(Clock), .D(Address[0]), .Q(out_5[0]), .en(Enable), .reset(Reset));  // open: Qn, preset
  D_Flip_Flop d_ff_2 (.clk(Clock), .D(Address[1]), .Q(out_5[1]), .en(Enable), .reset(Reset));  // open: Qn, preset
  D_Flip_Flop d_ff_3 (.clk(Clock), .D(Address[2]), .Q(out_5[2]), .en(Enable), .reset(Reset));  // open: Qn, preset
  D_Flip_Flop d_ff_4 (.clk(Clock), .D(Address[3]), .Q(out_5[3]), .en(Enable), .reset(Reset));  // open: Qn, preset
  D_Flip_Flop d_ff_5 (.clk(Clock), .D(Address[4]), .Q(out_5[4]), .en(Enable), .reset(Reset));  // open: Qn, preset
  D_Flip_Flop d_ff_6 (.clk(Clock), .D(Address[5]), .Q(out_5[5]), .en(Enable), .reset(Reset));  // open: Qn, preset
  D_Flip_Flop d_ff_7 (.clk(Clock), .D(Address[6]), .Q(out_5[6]), .en(Enable), .reset(Reset));  // open: Qn, preset
  D_Flip_Flop d_ff_8 (.clk(Clock), .D(Address[7]), .Q(out_5[7]), .en(Enable), .reset(Reset));  // open: Qn, preset
endmodule

// A
module Adder8b (
  input  [7:0] Address,
  input  [7:0] Jump,
  output [7:0] out_3,
  output out_4
);

  wire fa_1_out_5, fa_2_out_5, fa_3_out_5, fa_4_out_5, fa_5_out_5, fa_6_out_5, fa_7_out_5;

  FA fa_1 (.in_2(Address[0]), .in_3(Jump[0]), .in_1(1'b0), .out_5(fa_1_out_5), .out_4(out_3[0]));
  FA fa_2 (.in_2(Address[1]), .in_3(Jump[1]), .in_1(fa_1_out_5), .out_5(fa_2_out_5), .out_4(out_3[1]));
  FA fa_3 (.in_2(Address[2]), .in_3(Jump[2]), .in_1(fa_2_out_5), .out_5(fa_3_out_5), .out_4(out_3[2]));
  FA fa_4 (.in_2(Address[3]), .in_3(Jump[3]), .in_1(fa_3_out_5), .out_5(fa_4_out_5), .out_4(out_3[3]));
  FA fa_5 (.in_2(Address[4]), .in_3(Jump[4]), .in_1(fa_4_out_5), .out_5(fa_5_out_5), .out_4(out_3[4]));
  FA fa_6 (.in_2(Address[5]), .in_3(Jump[5]), .in_1(fa_5_out_5), .out_5(fa_6_out_5), .out_4(out_3[5]));
  FA fa_7 (.in_2(Address[6]), .in_3(Jump[6]), .in_1(fa_6_out_5), .out_5(fa_7_out_5), .out_4(out_3[6]));
  FA fa_8 (.in_2(Address[7]), .in_3(Jump[7]), .in_1(fa_7_out_5), .out_5(out_4), .out_4(out_3[7]));
endmodule

module MUX1b (
  input  in_1,
  input  in_2,
  input  in_3,
  output out_4
);

  wire and_1_out, and_2_out;

  and and_1 (and_1_out, in_1, ~in_3);  // AND_Gate
  and and_2 (and_2_out, in_2, in_3);
  or or_1 (out_4, and_1_out, and_2_out);
endmodule

// MUX
module MUX8b (
  input  [7:0] in_1,
  input  [7:0] in_2,
  input  in_3,
  output [7:0] out_4
);

  MUX1b mux1b_1 (.in_1(in_1[0]), .in_2(in_2[0]), .in_3(in_3), .out_4(out_4[0]));
  MUX1b mux1b_2 (.in_1(in_1[1]), .in_2(in_2[1]), .in_3(in_3), .out_4(out_4[1]));
  MUX1b mux1b_3 (.in_1(in_1[2]), .in_2(in_2[2]), .in_3(in_3), .out_4(out_4[2]));
  MUX1b mux1b_4 (.in_1(in_1[3]), .in_2(in_2[3]), .in_3(in_3), .out_4(out_4[3]));
  MUX1b mux1b_5 (.in_1(in_1[4]), .in_2(in_2[4]), .in_3(in_3), .out_4(out_4[4]));
  MUX1b mux1b_6 (.in_1(in_1[5]), .in_2(in_2[5]), .in_3(in_3), .out_4(out_4[5]));
  MUX1b mux1b_7 (.in_1(in_1[6]), .in_2(in_2[6]), .in_3(in_3), .out_4(out_4[6]));
  MUX1b mux1b_8 (.in_1(in_1[7]), .in_2(in_2[7]), .in_3(in_3), .out_4(out_4[7]));
endmodule

module BranchLogic (
  input  Branch,
  input  [7:0] Address,
  input  [7:0] Imm,
  output [7:0] out_4
);

  wire [7:0] mux8b_1_out_4;

  MUX8b mux8b_1 (.in_1(8'h1), .in_2(Imm), .in_3(Branch), .out_4(mux8b_1_out_4));
  Adder8b adder8b_1 (.Address(Address), .Jump(mux8b_1_out_4), .out_3(out_4));  // open: out_4
endmodule

module Registri (
  input  [1:0] ARS1,
  input  Reset,
  input  Clock,
  input  [7:0] RD,
  input  [1:0] ARS2,
  input  RegWrite,
  input  [1:0] ARD,
  output [7:0] RS1,
  output [7:0] RS2,
  output [7:0] x0,
  output [7:0] x1,
  output [7:0] x2,
  output [7:0] x3
);

  wire dex4_1_1_out_5, dex4_1_1_out_6, dex4_1_1_out_7;

  Reg u_x0 (.Address(RD), .Clock(Clock), .Enable(1'b0), .out_5(x0), .Reset(Reset));
  Reg u_x2 (.Address(RD), .Clock(Clock), .Enable(dex4_1_1_out_6), .out_5(x2), .Reset(Reset));
  DEX4_1 dex4_1_1 (
    .in_1(RegWrite), .in_2(ARD[1]), .in_3(ARD[0]), .out_5(dex4_1_1_out_5), .out_6(dex4_1_1_out_6),
    .out_7(dex4_1_1_out_7));  // open: out_4
  Reg u_x1 (.Address(RD), .Clock(Clock), .Enable(dex4_1_1_out_5), .out_5(x1), .Reset(Reset));
  Reg u_x3 (.Address(RD), .Clock(Clock), .Enable(dex4_1_1_out_7), .out_5(x3), .Reset(Reset));
  _4MUX8b u_4mux8b_1 (.in_1(x0), .in_2(x1), .in_3(x2), .in_4(x3), .in_5(ARS1), .out_6(RS1));
  _4MUX8b u_4mux8b_2 (.in_1(x0), .in_2(x1), .in_3(x2), .in_4(x3), .in_5(ARS2), .out_6(RS2));
endmodule

// MUX
module _4MUX8b (
  input  [7:0] in_1,
  input  [7:0] in_2,
  input  [7:0] in_3,
  input  [7:0] in_4,
  input  [1:0] in_5,
  output [7:0] out_6
);

  wire and_1_out;
  wire [7:0] mux8b_1_out_4, mux8b_2_out_4;

  MUX8b mux8b_1 (.in_1(in_1), .in_2(in_2), .in_3(in_5[0]), .out_4(mux8b_1_out_4));
  MUX8b mux8b_2 (.in_1(mux8b_1_out_4), .in_2(in_3), .in_3(in_5[1]), .out_4(mux8b_2_out_4));
  MUX8b mux8b_3 (.in_1(mux8b_2_out_4), .in_2(in_4), .in_3(and_1_out), .out_4(out_6));
  and and_1 (and_1_out, in_5[1], in_5[0]);
endmodule

// DEX
module DEX4_1 (
  input  in_1,
  input  in_2,
  input  in_3,
  output out_4,
  output out_5,
  output out_6,
  output out_7
);

  and and_1 (out_4, in_1, ~in_2, ~in_3);  // AND_Gate
  and and_2 (out_5, in_1, ~in_2, in_3);  // AND_Gate
  and and_3 (out_6, in_1, in_2, ~in_3);  // AND_Gate
  and and_4 (out_7, in_1, in_2, in_3);
endmodule

module ControlUnit (
  input  [15:0] in_1,
  output RegWrite,
  output [1:0] ARD,
  output [1:0] ARS1,
  output [1:0] ARS2,
  output [1:0] ALUctrl,
  output Branch,
  output ALUsrc,
  output MemR,
  output MemToReg,
  output MemW,
  output [7:0] Imm
);

  not not_1 (RegWrite, in_1[0]);
  ALUcontrol alucontrol_1 (
    .op1(in_1[0]), .op2(in_1[1]), .f31(in_1[4]), .f32(in_1[5]), .f71(in_1[10]), .f72(in_1[11]),
    .ALUC1(ALUctrl[0]), .ALUC2(ALUctrl[1]));
  Branch branch_1 (.out_3(Branch), .in_1(in_1[0]), .in_2(in_1[1]));
  _4MUX8b u_4mux8b_1 (
    .in_1(in_1[15:8]), .in_2({in_1[11], in_1[3], in_1[15:12], in_1[2], in_1[10]}), .in_3({8{1'b0}}),
    .in_4({in_1[15:10], in_1[3:2]}), .in_5(in_1[1:0]), .out_6(Imm));
  ALUsrc alusrc_1 (.out_3(ALUsrc), .in_1(in_1[0]), .in_2(in_1[1]));
  MemToReg memtoreg_1 (.out_3(MemR), .in_1(in_1[0]), .in_2(in_1[1]));
  MemW memw_1 (.out_3(MemW), .in_1(in_1[0]), .in_2(in_1[1]));

  assign ARD = in_1[3:2];
  assign ARS1 = in_1[7:6];
  assign ARS2 = in_1[9:8];
  assign MemToReg = MemR;

  // Other names for the same wires on the sheet: s0 = in_1[2]; sb1 = in_1[2]; s1 = in_1[3]; sb6 = in_1[3];
  //   l2 = in_1[10]; s2 = in_1[10]; sb0 = in_1[10]; l3 = in_1[11]; s3 = in_1[11]; sb7 = in_1[11]; l4 = in_1[12];
  //   s4 = in_1[12]; sb2 = in_1[12]; l5 = in_1[13]; s5 = in_1[13]; sb3 = in_1[13]; l6 = in_1[14]; s6 = in_1[14];
  //   sb4 = in_1[14]; l7 = in_1[15]; s7 = in_1[15]; sb5 = in_1[15]; l0 = in_1[8]; l1 = in_1[9]

  // Notes on the sheet:
  //   sb
  //   l
  //   s
endmodule

module Branch (
  input  in_1,
  input  in_2,
  output out_3
);

  and and_1 (out_3, in_1, ~in_2);  // AND_Gate
endmodule

module ALUsrc (
  input  in_1,
  input  in_2,
  output out_3
);

  wire and_1_out, and_2_out;

  and and_1 (and_1_out, ~in_1, ~in_2);  // AND_Gate
  and and_2 (and_2_out, in_1, in_2);
  or or_1 (out_3, and_1_out, and_2_out);
endmodule

module MemToReg (
  input  in_1,
  input  in_2,
  output out_3
);

  and and_1 (out_3, ~in_1, ~in_2);  // AND_Gate
endmodule

module MemW (
  input  in_1,
  input  in_2,
  output out_3
);

  and and_1 (out_3, in_1, in_2);
endmodule

// ALUctrl
module ALUcontrol (
  input  op1,
  input  op2,
  input  f31,
  input  f32,
  input  f71,
  input  f72,
  output ALUC1,
  output ALUC2
);

  wire and_1_out, and_2_out, and_3_out, and_4_out, and_5_out;

  and and_1 (and_1_out, op1, ~op2);  // AND_Gate
  and and_2 (and_2_out, ~op1, op2, ~f31, f32, ~f71, ~f72);  // AND_Gate
  and and_3 (and_3_out, ~op1, op2, ~f31, ~f32, f71, ~f72);  // AND_Gate
  and and_4 (and_4_out, ~op1, op2, ~f31, ~f32, ~f71, ~f72);  // AND_Gate
  and and_5 (and_5_out, op1, op2);
  or or_1 (ALUC1, and_1_out, and_3_out, and_2_out);
  or or_2 (ALUC2, ~op2, and_5_out, and_3_out, and_4_out);  // OR_Gate
endmodule

module ADD1b (
  input  Cin,
  input  A,
  input  B,
  input  nB,
  output S0,
  output Cout
);

  wire xor_1_out;

  xor xor_1 (xor_1_out, B, nB);
  FA fa_1 (.in_2(A), .in_3(xor_1_out), .in_1(Cin), .out_5(Cout), .out_4(S0));
endmodule

module ADD8b (
  input  Ci,
  input  [7:0] A,
  input  [7:0] B,
  output [7:0] out_4,
  output Co
);

  wire add1b_1_cout, add1b_2_cout, add1b_3_cout, add1b_4_cout, add1b_5_cout, add1b_6_cout, add1b_7_cout;

  ADD1b add1b_1 (.A(A[0]), .B(B[0]), .nB(Ci), .Cin(Ci), .Cout(add1b_1_cout), .S0(out_4[0]));
  ADD1b add1b_2 (.A(A[1]), .B(B[1]), .nB(Ci), .Cin(add1b_1_cout), .Cout(add1b_2_cout), .S0(out_4[1]));
  ADD1b add1b_3 (.A(A[2]), .B(B[2]), .nB(Ci), .Cin(add1b_2_cout), .Cout(add1b_3_cout), .S0(out_4[2]));
  ADD1b add1b_4 (.A(A[3]), .B(B[3]), .nB(Ci), .Cin(add1b_3_cout), .Cout(add1b_4_cout), .S0(out_4[3]));
  ADD1b add1b_5 (.A(A[4]), .B(B[4]), .nB(Ci), .Cin(add1b_4_cout), .Cout(add1b_5_cout), .S0(out_4[4]));
  ADD1b add1b_6 (.A(A[5]), .B(B[5]), .nB(Ci), .Cin(add1b_5_cout), .Cout(add1b_6_cout), .S0(out_4[5]));
  ADD1b add1b_7 (.A(A[6]), .B(B[6]), .nB(Ci), .Cin(add1b_6_cout), .Cout(add1b_7_cout), .S0(out_4[6]));
  ADD1b add1b_8 (.A(A[7]), .B(B[7]), .nB(Ci), .Cin(add1b_7_cout), .Cout(Co), .S0(out_4[7]));
endmodule

module ALU8b (
  input  [7:0] A,
  input  [7:0] B,
  input  [1:0] OP,
  output Zero,
  output [7:0] Out,
  output Co,
  output Over
);

  wire and_1_out;
  wire [7:0] add8b_1_out_4, and_2_out, mux8b_1_out_4, or_1_out;

  and and_1 (and_1_out, OP[1], OP[0]);
  ADD8b add8b_1 (.A(A), .B(B), .out_4(add8b_1_out_4), .Ci(and_1_out), .Co(Co));
  assign and_2_out = A & B;  // AND_Gate and_2, 8 bits wide
  assign or_1_out = A | B;  // OR_Gate or_1, 8 bits wide
  xor xor_1 (Over, Co, and_1_out);
  MUX8b mux8b_1 (.in_1(and_2_out), .in_2(or_1_out), .in_3(OP[0]), .out_4(mux8b_1_out_4));
  MUX8b mux8b_2 (.in_1(mux8b_1_out_4), .in_2(add8b_1_out_4), .in_3(OP[1]), .out_4(Out));
  nor nor_1 (Zero, Out[0], Out[1], Out[2], Out[3], Out[4], Out[5], Out[6], Out[7]);
endmodule
